# Fritzing sketch D1MiniMultipleReedSwitches (saved by Fritzing 0.9.3b)
circuit board: 8.46667cm x 5.64444cm
breadboards: 1

parts:
  WeMos_D1_Mini1 = WeMos D1 Mini
  R1 = Resistor [tolerance=±1% resistance=10k package="2512 [SMD]"]
  S3 = Reed switch [package=THT]
  S4 = Reed switch [package=THT]
  S1 = Reed switch [package=THT]
  R3 = Resistor [tolerance=±1% resistance=10k package="2512 [SMD]"]
  R4 = Resistor [tolerance=±1% resistance=10k package="2512 [SMD]"]
  R5 = Resistor [tolerance=±1% resistance=10k package="2512 [SMD]"]
  S5 = Reed switch [package=THT]
  S2 = Reed switch [package=THT]
  R2 = Resistor [tolerance=±1% resistance=10k package="2512 [SMD]"]

nets:
  N1: WeMos_D1_Mini1.5V, S3.pin_1, S4.pin_1, S1.pin_1, S5.pin_1, S2.pin_1
  N2: WeMos_D1_Mini1.D1, R5.Pin_1, S5.pin_2
  N3: WeMos_D1_Mini1.D2, S4.pin_2, R4.Pin_1
  N4: WeMos_D1_Mini1.D5, R1.Pin_1, S1.pin_2
  N5: WeMos_D1_Mini1.D6, S2.pin_2, R2.Pin_1
  N6: WeMos_D1_Mini1.D7, S3.pin_2, R3.Pin_1
  N7: WeMos_D1_Mini1.G, R1.Pin_0, R3.Pin_0, R4.Pin_0, R5.Pin_0, R2.Pin_0
